# Fritzing sketch car (saved by Fritzing 1.0.1rc)

parts:
  HC-SR04_Sensor_1 = HC-SR04 Ultrasonic Distance Sensor
  J1 = STM32 Nucleo boards
  Part1 = TB6612 DRV8833 Dual Motor Driver 1A TB6612FNG
  S1 = SPST Switch [package=r_sw_th]
  VCC1 = 4 x AAA Battery Mount
  M1 = gear-motor
  M2 = gear-motor
  VCC2 = Battery block 9V

nets:
  VCC: HC-SR04_Sensor_1.VCC, J1.5V
  N1: HC-SR04_Sensor_1.TRIG, J1.A5
  N2: HC-SR04_Sensor_1.ECHO, J1.D10_PWM/SS
  N3: J1.A0, Part1.STBY
  N4: J1.A1, Part1.AIN1
  N5: J1.A2, Part1.AIN2
  N6: J1.A3, Part1.BIN1
  N7: J1.A4, Part1.BIN2
  GND: J1.GND, Part1.GND, VCC1.-, VCC2.-
  N8: J1.VIN, VCC2.+
  N9: Part1.B01, M1.pin_1
  N10: Part1.B02, M1.pin_2
  N11: Part1.A02, M2.pin_1
  N12: Part1.A01, M2.pin_2
  N13: Part1.VM, S1.O
  N14: S1.S, VCC1.+

custom parts:
  STM32 Nucleo boards: The highly affordable STM32 Nucleo boards allow to try out new ideas and to quickly create prototypes with any STM32 MCU. Sharing Arduino connectors and ST Morpho headers, STM32 Nucleo boards can easily be extended with a large number of application related hardware add-ons. The STM32 Nucleo boards come with an integrated ST-Link debugger/programmer; no need for an external probe. The boards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
  TB6612 DRV8833 Dual Motor Driver 1A TB6612FNG: Modified: VCC, PWMA, PWMB -> NC The TB6612FNG motor driver can control up to two DC motors at a constant current of 1.2A (3.2A peak). Two input signals (IN1 and IN2) can be used to control the motor in one of four function modes - CW, CCW, short-brake, and stop. The two motor outputs (A and B) can be separately controlled, the speed of each motor is controlled via a PWM input signal with a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
